// Logisim project lab3 cao.circ as structural Verilog: 1 circuit, main circuit main
module main (
  input  in_1,
  input  in_2,
  input  in_3
);

  wire clock_1_out;
  wire [6:0] bit_extender_1_out;
  wire [7:0] ram_1_data, random_1_out;

  Clock clock_1 (.out(clock_1_out));
  Random random_1 (.clk(clock_1_out), .out(random_1_out), .clr(in_2));  // open: next
  RAM ram_1 (.addr(random_1_out), .data(ram_1_data), .sel(in_1));  // open: clk, ld, clr
  Bit_Extender #(.out_width(7), .\type ("one")) bit_extender_1 (.in(ram_1_data), .out(bit_extender_1_out));
  TTY tty_1 (.data(bit_extender_1_out), .clk(clock_1_out), .we(in_3));  // open: clr
endmodule
